# Fritzing sketch thermocouple (saved by Fritzing 0.9.3b)
breadboards: 1

parts:
  Part1 = Arduino Uno (Rev3)
  LCD1 = LCD screen
  Part3 = Adafruit Thermocouple Amplifier MAX31855 [part_number="Adafruit #269"]
  R1 = Trimmer Potentiometer [maximum_resistance=10kΩ package=THT]

nets:
  N1: Part1.D8, LCD1.E
  N2: Part1.D9_PWM, LCD1.DB4
  N3: Part1.D10_PWM/SS, LCD1.DB5
  N4: Part1.D11_PWM/MOSI, LCD1.DB6
  N5: Part1.D12/MISO, LCD1.DB7
  GND: Part1.GND, LCD1.VSS, LCD1.LED+, Part3.GND, R1.leg2
  N6: Part1.D3_PWM, Part3.DO
  N7: Part1.D4, Part3.CS
  N8: Part1.D5_PWM, Part3.CLK
  N9: Part1.D7, LCD1.R/W
  3V3: Part1.3V3, Part3.VIN, Part3.+3V3
  5V: Part1.5V, LCD1.VDD, LCD1.RS, LCD1.LED-, R1.leg1
  N10: LCD1.V0, R1.wiper

custom parts:
  Adafruit Thermocouple Amplifier MAX31855: Thermocouples are very sensitive, requiring a good amplifier with a cold-compensation reference. The MAX31855K does everything for you, and can be easily interfaced with any microcontroller, even one without an analog input. This breakout board has the chip itself, a 3.3V regulator with 10uF bypass capacitors and level shifting circuitry, all assembled and tested. Comes with a 2 pin terminal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
